# Fritzing sketch nfc_locker(Uno) (saved by Fritzing 0.9.5d)

parts:
  Arduino_Uno = Arduino Uno (Rev3) - ICSP
  Elechouse_PN532_NFC_RFID_Module_V3 = PN532 Elechouse RFID NFC Module V3

nets:
  N1: Arduino_Uno.A4/SDA, Elechouse_PN532_NFC_RFID_Module_V3.SDA
  N2: Arduino_Uno.A5/SCL, Elechouse_PN532_NFC_RFID_Module_V3.SCL
  5V: Arduino_Uno.5V, Elechouse_PN532_NFC_RFID_Module_V3.VCC
  GND: Arduino_Uno.GND, Elechouse_PN532_NFC_RFID_Module_V3.GND

notes:
  The PN532 module needs its DIP switches set for I2C
  Channel 1 = On
  Channel 2 = Off

custom parts:
  PN532 Elechouse RFID NFC Module V3: NFC is a popular technology in recent years. We often heard this work while smart phone company such as Samsung or HTC introduces their latest high-end phones. Almost all the high-end phone in the market support NFC. Near field communication (NFC) is a set of standards for smart phones and similar devices to establish radio communication with each other by touching them together or bringing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
